// Logisim project LED traffic light.circ as structural Verilog: 1 circuit, main circuit main
module main (
  input  in_1
);

  wire button_1_out, clock_1_out;
  wire [1:0] rom_2_data;
  wire [2:0] rom_1_data;
  wire [3:0] counter_1_q, counter_2_q;

  LED led_1 (.in(in_1));
  LED led_2 (.in(in_1));
  LED led_3 (.in(in_1));
  Clock clock_1 (.out(clock_1_out));
  Counter #(.width(4), .max('hf), .behavior("old")) counter_1 (
    .count(clock_1_out), .Q(counter_1_q), .clk(clock_1_out), .clr(button_1_out));  // open: load, D, carry, preset
  Button button_1 (.out(button_1_out));
  Counter #(.width(4), .max('hf), .behavior("old")) counter_2 (
    .count(clock_1_out), .Q(counter_2_q), .clk(clock_1_out), .clr(button_1_out));  // open: load, D, carry, preset
  ROM #(.addrWidth(4), .dataWidth(3), .Select("low")) rom_1 (.addr(counter_1_q), .data(rom_1_data));
  ROM #(.addrWidth(4), .dataWidth(2), .Select("low")) rom_2 (.addr(counter_2_q), .data(rom_2_data));
  LED led_4 (.in(rom_2_data[1]));
  LED led_5 (.in(rom_2_data[0]));
  LED led_6 (.in(rom_1_data[0]));
  LED led_7 (.in(rom_1_data[1]));
  LED led_8 (.in(rom_1_data[2]));
  // RGBLed rgbled_1: pin names not known; wires that end beside it: rom_2_data[1], rom_2_data[0]
  // RGBLed rgbled_2: pin names not known; wires that end beside it: rom_1_data[0], rom_1_data[2]

  // Notes on the sheet:
  //   reset
  //   LED TRAFFIC LIGHT
  //   contents of rom_2 (hex, n*v repeats v):
  //   6*1 10*2
  //   PEDESTRIAN STATUS
  //   BY ABHEESHT MISHRA
  //   220291520008
  //   TRAFFIC STATUS
endmodule
